// Logisim project CC4N-CPU.circ as structural Verilog: 16 circuits, main circuit main
module main (
);

  wire clock_1_out, not_1_out, not_2_out, O_q, RESET_out, uc_1_ac, uc_1_e, uc_1_ir, uc_1_load, uc_1_pc,
       uc_1_pc_rest, uc_1_r_1_w_0, uc_1_ram, ula_1_overflow, ula_1_zero, Z_q;
  wire [2:0] uc_1_opcode;
  wire [3:0] ac_1_s, counter_1_q, mux_1_out_4, ram_1_data, uc_1_dados, uc_1_operando, ula_1_s;
  wire [7:0] ir_1_s, rom_1_data;

  not not_1 (not_1_out, uc_1_load);
  Counter #(.width(4), .max('hf), .trigger("falling")) counter_1 (
    .load(uc_1_load), .D(uc_1_dados), .count(not_1_out), .Q(counter_1_q), .clk(uc_1_pc), .clr(uc_1_pc_rest));  // open: carry
  Clock clock_1 (.out(clock_1_out));
  Button RESET (.out(RESET_out));
  UC uc_1 (
    .\INSTRUÇÃO (ir_1_s), .Clock(clock_1_out), .Operando(uc_1_operando), .E(uc_1_e), .OPCODE(uc_1_opcode),
    .IR(uc_1_ir), .PC(uc_1_pc), .AC(uc_1_ac), .RAM(uc_1_ram), .PC_REST(uc_1_pc_rest), .RESET(RESET_out),
    .R_1_W_0(uc_1_r_1_w_0), .Dados(uc_1_dados), .Zero(Z_q), .Overflow(O_q), .Load(uc_1_load));
  ROM #(.addrWidth(4)) rom_1 (.addr(counter_1_q), .data(rom_1_data));  // open: sel
  IR ir_1 (.in_1(uc_1_ir), .S(ir_1_s), .E(rom_1_data));
  MUX mux_1 (.C(uc_1_e), .E(uc_1_operando), .D(ram_1_data), .out_4(mux_1_out_4));
  ULA ula_1 (
    .D(uc_1_e), .A(ac_1_s), .B(mux_1_out_4), .in_4(uc_1_opcode), .Zero(ula_1_zero),
    .Overflow(ula_1_overflow), .S(ula_1_s));
  AC ac_1 (.Clock(uc_1_ac), .E(ula_1_s), .S(ac_1_s));
  // Probe on mux_1_out_4
  // Probe on ula_1_s
  // Probe on ac_1_s
  D_Flip_Flop Z (.clk(uc_1_ac), .D(ula_1_zero), .Q(Z_q));  // open: Qn, preset, en, reset
  D_Flip_Flop O (.clk(uc_1_ac), .D(ula_1_overflow), .Q(O_q));  // open: Qn, preset, en, reset
  RAM #(.addrWidth(4), .dataWidth(4)) ram_1 (
    .addr(uc_1_operando), .data(ram_1_data), .clk(uc_1_ram), .ld(uc_1_r_1_w_0));  // open: sel, clr
  not not_2 (not_2_out, uc_1_r_1_w_0);
  Buffer buffer_1 (.E(ac_1_s), .C(not_2_out), .S(ram_1_data));

  // Notes on the sheet:
  //   contents of rom_1 (hex, n*v repeats v):
  //   1 f0 1 f1 10 31 d0 f2 11 f0 12 f1 e4
  //   3
  //   4
  //   5
  //   7
  //   8
  //   C
  //   F
  //   0
  //   0
  //   MOV
  //   000
  //   1
  //   1
  //   000
  //   MOV
  //   0
  //   001
  //   ADD
  //   2
  //   1
  //   001
  //   ADD
  //   0
  //   SUB
  //   010
  //   010
  //   1
  //   SUB
  //   0
  //   6
  //   011
  //   OR
  //   1
  //   OR
  //   011
  //   0
  //   NOT
  //   100
  //   100
  //   NOT
  //   1
  //   9
  //   0
  //   101
  //   SHF
  //   A
  //   1
  //   B
  //   SHF
  //   101
  //   JPZ
  //   110
  //   0
  //   JPO
  //   110
  //   1
  //   D
  //   111
  //   GO
  //   0
  //   E
  //   STR
  //   1
  //   111
  //   Instruction Set
  //   AC <= X
  //   AC <= M(X)
  //   AC <= AC+X
  //   AC <= AC+M(X)
  //   AC <= AC-X
  //   AC <= AC-M(X)
  //   AC <= AC OR X
  //   AC <= AC OR M(X)
  //   AC <= NOT X
  //   AC <= NOT M( X)
  //   AC <= AC << Q
  //   AC <= AC >> Q
  //   PC <= X SE FLAG Z
  //   PC <= X SE FLAG O
  //   PC <= X
  //   M(X) <= AC 
endmodule

module ULA (
  input  D,
  input  [3:0] A,
  input  [3:0] B,
  input  [2:0] in_4,
  output Overflow,
  output [3:0] S,
  output Zero
);

  wire add_4_1_out_3, and_1_out, and_2_out, deco_1_d0, deco_1_d1, deco_1_d2, deco_1_d3, deco_1_d4, deco_1_d5,
       deco_1_d6, deco_1_d7, not_2_out, sub_4_1_overflow;
  wire [3:0] add_4_1_out_4, buffer_7_s, not_1_s, or_2_s, rot_d_1_abcd_2, rot_e_1_abcd_2, sub_4_1_s;

  or or_1 (Overflow, and_1_out, and_2_out);
  Deco deco_1 (
    .D0(deco_1_d0), .D1(deco_1_d1), .D2(deco_1_d2), .D3(deco_1_d3), .D4(deco_1_d4), .D5(deco_1_d5),
    .D6(deco_1_d6), .D7(deco_1_d7), .A_B_C(in_4));
  and and_1 (and_1_out, deco_1_d2, sub_4_1_overflow);
  and and_2 (and_2_out, add_4_1_out_3, deco_1_d1);
  Buffer buffer_1 (.E(B), .C(deco_1_d0), .S(S));
  ADD_4 add_4_1 (.in_2(B), .out_3(add_4_1_out_3), .in_1(A), .out_4(add_4_1_out_4));
  // Probe on add_4_1_out_4
  Buffer buffer_2 (.E(add_4_1_out_4), .C(deco_1_d1), .S(S));
  // Probe on sub_4_1_s
  nor nor_1 (Zero, S[0], S[1], S[2], S[3], deco_1_d6, deco_1_d7);
  Sub_4 sub_4_1 (.A(A), .Overflow(sub_4_1_overflow), .B(B), .S(sub_4_1_s));
  Buffer buffer_3 (.E(sub_4_1_s), .C(deco_1_d2), .S(S));
  NOT not_1 (.E(B), .S(not_1_s));
  OR or_2 (.A(A), .B(B), .S(or_2_s));
  Buffer buffer_4 (.E(or_2_s), .C(deco_1_d3), .S(S));
  Buffer buffer_5 (.E(not_1_s), .C(deco_1_d4), .S(S));
  Rot_E rot_e_1 (.abcd(A), .xy(B[1:0]), .ABCD_2(rot_e_1_abcd_2));
  Rot_D rot_d_1 (.abcd(A), .xy(B[1:0]), .ABCD_2(rot_d_1_abcd_2));
  Buffer buffer_6 (.E(buffer_7_s), .C(deco_1_d5), .S(S));
  Buffer buffer_7 (.E(rot_d_1_abcd_2), .C(D), .S(buffer_7_s));
  not not_2 (not_2_out, D);
  Buffer buffer_8 (.E(rot_e_1_abcd_2), .C(not_2_out), .S(buffer_7_s));
endmodule

module ADD_1 (
  input  A,
  input  B,
  input  C,
  output S,
  output Vai_1
);

  wire and_1_out, and_2_out, or_1_out, xor_1_out;

  xor xor_1 (xor_1_out, B, C);
  or or_1 (or_1_out, B, C);
  and and_1 (and_1_out, B, C);
  xor xor_2 (S, xor_1_out, A);
  and and_2 (and_2_out, or_1_out, A);
  or or_2 (Vai_1, and_2_out, and_1_out);
endmodule

module ADD_4 (
  input  [3:0] in_1,
  input  [3:0] in_2,
  output out_3,
  output [3:0] out_4
);

  wire add_1_2_vai_1, add_1_3_vai_1, add_1_4_vai_1;

  // Probe on in_2
  ADD_1 add_1_1 (.Vai_1(out_3), .A(in_2[3]), .B(in_1[3]), .C(add_1_2_vai_1), .S(out_4[3]));
  ADD_1 add_1_2 (.Vai_1(add_1_2_vai_1), .A(in_2[2]), .B(in_1[2]), .C(add_1_3_vai_1), .S(out_4[2]));
  // Probe on out_4
  // Probe on in_1
  ADD_1 add_1_3 (.Vai_1(add_1_3_vai_1), .A(in_2[1]), .B(in_1[1]), .C(add_1_4_vai_1), .S(out_4[1]));
  ADD_1 add_1_4 (.Vai_1(add_1_4_vai_1), .A(in_2[0]), .B(in_1[0]), .C(1'b0), .S(out_4[0]));
endmodule

module Sub_1 (
  input  A,
  input  B,
  input  C,
  output S,
  output Vai_1
);

  wire and_1_out, and_2_out, not_1_out, or_1_out, xor_1_out;

  xor xor_1 (xor_1_out, B, C);
  or or_1 (or_1_out, B, C);
  not not_1 (not_1_out, A);
  and and_1 (and_1_out, B, C);
  xor xor_2 (S, xor_1_out, A);
  and and_2 (and_2_out, or_1_out, not_1_out);
  or or_2 (Vai_1, and_2_out, and_1_out);
endmodule

module Sub_4 (
  input  [3:0] B,
  input  [3:0] A,
  output Overflow,
  output [3:0] S
);

  wire sub_1_2_vai_1, sub_1_3_vai_1, sub_1_4_vai_1;

  // Probe on A
  Sub_1 sub_1_1 (.Vai_1(Overflow), .A(A[3]), .B(B[3]), .C(sub_1_2_vai_1), .S(S[3]));
  Sub_1 sub_1_2 (.Vai_1(sub_1_2_vai_1), .A(A[2]), .B(B[2]), .C(sub_1_3_vai_1), .S(S[2]));
  Sub_1 sub_1_3 (.Vai_1(sub_1_3_vai_1), .A(A[1]), .B(B[1]), .C(sub_1_4_vai_1), .S(S[1]));
  // Probe on S
  Sub_1 sub_1_4 (.Vai_1(sub_1_4_vai_1), .A(A[0]), .B(B[0]), .C(1'b0), .S(S[0]));
  // Probe on B
endmodule

module Rot_E (
  input  [3:0] abcd,
  input  [1:0] xy,
  output [3:0] ABCD_2
);

  wire and_1_out, and_2_out, and_3_out, and_4_out, and_5_out, and_6_out, and_7_out, and_8_out, and_9_out;

  and and_1 (and_1_out, abcd[3], ~xy[1], ~xy[0]);  // AND_Gate
  and and_2 (and_2_out, abcd[2], ~xy[1], xy[0]);  // AND_Gate
  and and_3 (and_3_out, abcd[1], xy[1], ~xy[0]);  // AND_Gate
  and and_4 (and_4_out, abcd[0], xy[1], xy[0]);
  and and_5 (and_5_out, abcd[2], ~xy[1], ~xy[0]);  // AND_Gate
  and and_6 (and_6_out, abcd[1], ~xy[1], xy[0]);  // AND_Gate
  and and_7 (and_7_out, abcd[0], xy[1], ~xy[0]);  // AND_Gate
  and and_8 (and_8_out, abcd[1], ~xy[1], ~xy[0]);  // AND_Gate
  and and_9 (and_9_out, abcd[0], ~xy[1], xy[0]);  // AND_Gate
  and and_10 (ABCD_2[0], abcd[0], ~xy[1], ~xy[0]);  // AND_Gate
  or or_1 (ABCD_2[1], and_8_out, and_9_out);
  or or_2 (ABCD_2[3], and_1_out, and_2_out, and_3_out, and_4_out);
  or or_3 (ABCD_2[2], and_5_out, and_6_out, and_7_out);
endmodule

module Rot_D (
  input  [3:0] abcd,
  input  [1:0] xy,
  output [3:0] ABCD_2
);

  wire and_1_out, and_2_out, and_3_out, and_4_out, and_5_out, and_6_out, and_7_out, and_8_out, and_9_out;

  and and_1 (and_1_out, abcd[0], ~xy[1], ~xy[0]);  // AND_Gate
  and and_2 (and_2_out, abcd[1], ~xy[1], xy[0]);  // AND_Gate
  and and_3 (and_3_out, abcd[2], xy[1], ~xy[0]);  // AND_Gate
  and and_4 (and_4_out, abcd[3], xy[1], xy[0]);
  and and_5 (and_5_out, abcd[1], ~xy[1], ~xy[0]);  // AND_Gate
  and and_6 (and_6_out, abcd[2], ~xy[1], xy[0]);  // AND_Gate
  and and_7 (and_7_out, abcd[3], xy[1], ~xy[0]);  // AND_Gate
  and and_8 (and_8_out, abcd[2], ~xy[1], ~xy[0]);  // AND_Gate
  and and_9 (and_9_out, abcd[3], ~xy[1], xy[0]);  // AND_Gate
  and and_10 (ABCD_2[3], abcd[3], ~xy[1], ~xy[0]);  // AND_Gate
  or or_1 (ABCD_2[2], and_8_out, and_9_out);
  or or_2 (ABCD_2[0], and_1_out, and_2_out, and_3_out, and_4_out);
  or or_3 (ABCD_2[1], and_5_out, and_6_out, and_7_out);
endmodule

module Deco (
  input  [2:0] A_B_C,
  output D0,
  output D1,
  output D2,
  output D3,
  output D4,
  output D5,
  output D6,
  output D7
);

  wire not_1_out, not_2_out, not_3_out, not_4_out, not_5_out, not_6_out, not_7_out, not_8_out, not_9_out,
       not_10_out, not_11_out, not_12_out;

  not not_1 (not_1_out, A_B_C[2]);
  not not_2 (not_2_out, A_B_C[1]);
  not not_3 (not_3_out, A_B_C[0]);
  not not_4 (not_4_out, A_B_C[2]);
  not not_5 (not_5_out, A_B_C[1]);
  not not_6 (not_6_out, A_B_C[2]);
  not not_7 (not_7_out, A_B_C[0]);
  not not_8 (not_8_out, A_B_C[2]);
  not not_9 (not_9_out, A_B_C[1]);
  not not_10 (not_10_out, A_B_C[0]);
  not not_11 (not_11_out, A_B_C[1]);
  not not_12 (not_12_out, A_B_C[0]);
  and and_1 (D7, A_B_C[2], A_B_C[1], A_B_C[0]);
  and and_2 (D0, not_1_out, not_2_out, not_3_out);
  and and_3 (D1, not_4_out, not_5_out, A_B_C[0]);
  and and_4 (D2, not_6_out, A_B_C[1], not_7_out);
  and and_5 (D3, not_8_out, A_B_C[1], A_B_C[0]);
  and and_6 (D4, A_B_C[2], not_9_out, not_10_out);
  and and_7 (D5, A_B_C[2], not_11_out, A_B_C[0]);
  and and_8 (D6, A_B_C[2], A_B_C[1], not_12_out);
endmodule

module Buffer (
  input  [3:0] E,
  input  C,
  output [3:0] S
);

  assign S[3] = C ? E[3] : 1'bz;  // Controlled_Buffer controlled_buffer_1
  assign S[1] = C ? E[1] : 1'bz;  // Controlled_Buffer controlled_buffer_2
  assign S[2] = C ? E[2] : 1'bz;  // Controlled_Buffer controlled_buffer_3
  assign S[0] = C ? E[0] : 1'bz;  // Controlled_Buffer controlled_buffer_4
endmodule

module NOT (
  input  [3:0] E,
  output [3:0] S
);

  not not_1 (S[3], E[3]);
  not not_2 (S[1], E[1]);
  not not_3 (S[2], E[2]);
  not not_4 (S[0], E[0]);
endmodule

module OR (
  input  [3:0] B,
  input  [3:0] A,
  output [3:0] S
);

  // Probe on A
  or or_1 (S[3], A[3], B[3]);
  or or_2 (S[2], A[2], B[2]);
  or or_3 (S[1], A[1], B[1]);
  // Probe on S
  or or_4 (S[0], A[0], B[0]);
  // Probe on B
endmodule

module AC (
  input  Clock,
  input  [3:0] E,
  output [3:0] S
);

  D_Flip_Flop d_ff_1 (.clk(Clock), .D(E[3]), .Q(S[3]));  // open: Qn, preset, en, reset
  D_Flip_Flop d_ff_2 (.clk(Clock), .D(E[2]), .Q(S[2]));  // open: Qn, preset, en, reset
  D_Flip_Flop d_ff_3 (.clk(Clock), .D(E[1]), .Q(S[1]));  // open: Qn, preset, en, reset
  D_Flip_Flop d_ff_4 (.clk(Clock), .D(E[0]), .Q(S[0]));  // open: Qn, preset, en, reset
endmodule

module MUX (
  input  [3:0] E,
  input  [3:0] D,
  input  C,
  output [3:0] out_4
);

  wire not_1_out;

  not not_1 (not_1_out, C);
  Buffer buffer_1 (.E(E), .C(not_1_out), .S(out_4));
  Buffer buffer_2 (.E(D), .C(C), .S(out_4));
endmodule

module IR (
  input  in_1,
  input  [7:0] E,
  output [7:0] S
);

  D_Flip_Flop #(.trigger("falling")) d_ff_1 (.clk(in_1), .D(E[7]), .Q(S[7]));  // open: Qn, preset, en, reset
  D_Flip_Flop #(.trigger("falling")) d_ff_2 (.clk(in_1), .D(E[6]), .Q(S[6]));  // open: Qn, preset, en, reset
  D_Flip_Flop #(.trigger("falling")) d_ff_3 (.clk(in_1), .D(E[5]), .Q(S[5]));  // open: Qn, preset, en, reset
  D_Flip_Flop #(.trigger("falling")) d_ff_4 (.clk(in_1), .D(E[4]), .Q(S[4]));  // open: Qn, preset, en, reset
  D_Flip_Flop #(.trigger("falling")) d_ff_5 (.clk(in_1), .D(E[3]), .Q(S[3]));  // open: Qn, preset, en, reset
  D_Flip_Flop #(.trigger("falling")) d_ff_6 (.clk(in_1), .D(E[2]), .Q(S[2]));  // open: Qn, preset, en, reset
  D_Flip_Flop #(.trigger("falling")) d_ff_7 (.clk(in_1), .D(E[1]), .Q(S[1]));  // open: Qn, preset, en, reset
  D_Flip_Flop #(.trigger("falling")) d_ff_8 (.clk(in_1), .D(E[0]), .Q(S[0]));  // open: Qn, preset, en, reset
endmodule

module UC (
  input  [7:0] \INSTRUÇÃO ,
  input  Clock,
  input  RESET,
  input  Overflow,
  input  Zero,
  output [3:0] Dados,
  output [3:0] Operando,
  output E,
  output IR,
  output PC,
  output RAM,
  output [2:0] OPCODE,
  output PC_REST,
  output AC,
  output R_1_W_0,
  output Load
);

  wire GOTO_out, JPO_out, JPZ_out;
  wire [1:0] counter_1_q;

  Counter #(.width(2), .max('h3)) counter_1 (.Q(counter_1_q), .clk(Clock), .clr(RESET));  // open: load, D, count, carry
  and and_1 (AC, counter_1_q[1], ~counter_1_q[0]);  // AND_Gate
  and and_2 (PC, ~counter_1_q[1], counter_1_q[0]);  // AND_Gate
  and and_3 (IR, ~counter_1_q[1], ~counter_1_q[0]);  // AND_Gate
  and JPO (JPO_out, \INSTRUÇÃO [7], \INSTRUÇÃO [6], ~\INSTRUÇÃO [5], \INSTRUÇÃO [4], PC, Overflow);  // AND_Gate
  and and_4 (RAM, counter_1_q[1], counter_1_q[0]);
  and JPZ (JPZ_out, \INSTRUÇÃO [7], \INSTRUÇÃO [6], ~\INSTRUÇÃO [5], ~\INSTRUÇÃO [4], PC, Zero);  // AND_Gate
  or or_1 (Load, JPO_out, JPZ_out, GOTO_out);
  and GOTO (GOTO_out, \INSTRUÇÃO [7], \INSTRUÇÃO [6], \INSTRUÇÃO [5], ~\INSTRUÇÃO [4], PC);  // AND_Gate
  nand R_W (R_1_W_0, AC, \INSTRUÇÃO [7], \INSTRUÇÃO [6], \INSTRUÇÃO [5], \INSTRUÇÃO [4]);

  assign Dados = \INSTRUÇÃO [3:0];
  assign E = \INSTRUÇÃO [4];
  assign OPCODE = \INSTRUÇÃO [7:5];
  assign Operando = \INSTRUÇÃO [3:0];
  assign PC_REST = RESET;
endmodule
